# Fritzing sketch Sedu_Pinball_Circuit (saved by Fritzing 0.9.4)
breadboards: 1

parts:
  Part1 = Arduino Nano (Rev3.0)
  R1 = PHOTOCELL [package=photocell-kit]
  J1 = Basic Servo
  J2 = Basic Servo
  U1 = 7-SEGMENT-4DIGIT [package=7-segment-4digit]
  S1 = SWITCH-MOMENTARY-2 [package=tactile_switch_tall]
  S2 = SWITCH-MOMENTARY-2 [package=tactile_switch_tall]
  BAT1 = BC9VPC [package=bc9vpc]

nets:
  GND: Part1.GND, R1.P$1, J1.gnd, J2.gnd, S1.2, S2.2, BAT1.V-
  N1: Part1.D3, J2.pulse
  N2: Part1.D4, S1.1
  N3: Part1.D5, J1.pulse
  N4: Part1.D6, S2.1
  N5: Part1.D7, U1.16
  N6: Part1.D8, U1.15
  N7: Part1.D9, U1.14
  N8: Part1.D10, U1.13
  N9: Part1.D11/MOSI, U1.1
  N10: Part1.D12/MISO, U1.2
  N11: Part1.VIN, BAT1.V+
  VCC: Part1.5V, J1.vcc, J2.vcc
  N12: Part1.A6, U1.8
  N13: Part1.A5, U1.7
  N14: Part1.A4, U1.6
  N15: Part1.A3, U1.5
  N16: Part1.A2, U1.4
  N17: Part1.A1, U1.3
  N18: Part1.A0, R1.P$2
